// Digital circuit lab04_sub.dig as structural Verilog
// COMP1003 Lab 04 Exercise 4: 4-bit ALU.\na,b: 4-bit operands. op: 1 bit. fun: 3 bits. cin: status in.\nout: 4-bit result. cout: status out, carry of addition only.\nop fun | operation\n0 000 | a+b+cin\n0 001 | low 4 bits of a*b\n0 010 | a-b-cin\n1 000 | signed compare: bit0 a>b, bit1 a=b, bit2 a<b\n1 001 | logical shift right of a by b\n1 010 | logical shift left of a by b\n1 011 | unsigned compare, same bit encoding
module lab04_sub (
  input  [3:0] a,
  input  [3:0] b,
  input  op,
  input  [2:0] fun,
  input  cin,
  output [3:0] out,
  output cout
);

  wire add_co, n_f0, n_f1, n_f2, n_op;
  wire [2:0] cmp_s, cmp_u;
  wire [3:0] diff, mul, sll, sll_raw, srl, srl_raw, sum, y0, y1;
  wire [7:4] mul_1_mul;

  BarrelShifter #(.Bits(4)) barrelshifter_1 (.in(a), .shift(b[2:0]), .out(sll_raw));
  BarrelShifter #(.Bits(4), .direction("right")) barrelshifter_2 (.in(a), .shift(b[2:0]), .out(srl_raw));
  not not_1 (n_op, op);
  not not_2 (n_f0, fun[0]);
  not not_3 (n_f1, fun[1]);
  not not_4 (n_f2, fun[2]);
  Multiplexer #(.Bits(4), .Selector_Bits(1)) multiplexer_1 (.sel(b[3]), .in_0(sll_raw), .in_1(4'b0000), .out(sll));
  Multiplexer #(.Bits(4), .Selector_Bits(1)) multiplexer_2 (.sel(b[3]), .in_0(srl_raw), .in_1(4'b0000), .out(srl));
  Add #(.Bits(4)) add_1 (.a(a), .b(b), .c_i(cin), .s(sum), .c_o(add_co));
  Sub #(.Bits(4)) sub_1 (.a(a), .b(b), .c_i(cin), .s(diff));  // open: c_o
  Mul #(.Bits(4)) mul_1 (.a(a), .b(b), .mul({mul_1_mul, mul}));
  Comparator #(.Bits(4), .Signed("true")) comparator_1 (.a(a), .b(b), .gt(cmp_s[0]), .eq(cmp_s[1]), .lt(cmp_s[2]));
  Comparator #(.Bits(4), .Signed("false")) comparator_2 (.a(a), .b(b), .gt(cmp_u[0]), .eq(cmp_u[1]), .lt(cmp_u[2]));
  Multiplexer #(.Bits(4), .Selector_Bits(3)) multiplexer_3 (
    .sel(fun), .in_0(sum), .in_1(mul), .in_2(diff), .in_3(4'b0000), .in_4(4'b0000), .in_5(4'b0000),
    .in_6(4'b0000), .in_7(4'b0000), .out(y0));
  Multiplexer #(.Bits(4), .Selector_Bits(3)) multiplexer_4 (
    .sel(fun), .in_0({1'b0, cmp_s}), .in_1(srl), .in_2(sll), .in_3({1'b0, cmp_u}), .in_4(4'b0000),
    .in_5(4'b0000), .in_6(4'b0000), .in_7(4'b0000), .out(y1));
  and and_1 (cout, n_op, n_f0, n_f1, n_f2, add_co);
  Multiplexer #(.Bits(4), .Selector_Bits(1)) multiplexer_5 (.sel(op), .in_0(y0), .in_1(y1), .out(out));

  // Other names for the same wires on the sheet: b_lo[2:0] = b[2:0]; b_hi = b[3]; eq_s = cmp_s[1]; eq_u = cmp_u[1];
  //   f0 = fun[0]; f1 = fun[1]; f2 = fun[2]; gt_s = cmp_s[0]; gt_u = cmp_u[0]; lt_s = cmp_s[2]; lt_u = cmp_u[2];
  //   Y[3:0] = out
endmodule

/* Test case ALU:
a b op fun cin out cout
5 3 0 0 0 8 0
15 1 0 0 0 0 1
15 1 0 0 1 1 1
7 7 0 0 1 15 0
0 0 0 0 1 1 0
15 15 0 1 0 1 0
10 3 0 1 1 14 0
7 2 0 1 0 14 0
5 3 0 2 0 2 0
5 3 0 2 1 1 0
3 5 0 2 0 14 0
0 0 0 2 1 15 0
5 3 1 0 0 1 0
3 5 1 0 0 4 0
5 5 1 0 0 2 0
1 15 1 0 0 1 0
15 1 1 0 0 4 0
8 7 1 0 0 4 0
8 1 1 1 0 4 0
8 3 1 1 0 1 0
15 1 1 1 0 7 0
15 4 1 1 0 0 0
10 0 1 1 0 10 0
1 2 1 1 0 0 0
1 1 1 2 0 2 0
1 3 1 2 0 8 0
3 2 1 2 0 12 0
1 4 1 2 0 0 0
8 1 1 2 0 0 0
15 0 1 2 0 15 0
5 3 1 3 0 1 0
3 5 1 3 0 4 0
5 5 1 3 0 2 0
1 15 1 3 0 4 0
15 1 1 3 0 1 0
8 7 1 3 0 1 0
15 1 0 3 0 0 0
15 1 1 4 0 0 0
9 1 1 1 0 4 0
6 1 1 2 0 12 0
6 2 1 2 0 8 0
6 5 1 2 0 0 0
6 8 1 2 0 0 0
*/
