// Digital circuit lab05_sub.dig as structural Verilog
// 4 x 4-bit register file. WE writes Din at WL on the rising edge of c. clr asynchronously clears every register. RE drives Dout from RL, otherwise Dout is high-Z.
module lab05_sub (
  input  c,
  input  clr,
  input  WE,
  input  [1:0] WL,
  input  [3:0] Din,
  input  RE,
  input  [1:0] RL,
  output [3:0] Dout
);

  wire clk, demultiplexer_1_out_0, demultiplexer_1_out_1, demultiplexer_1_out_2, demultiplexer_1_out_3,
       or_2_out, or_3_out, or_4_out, or_5_out;
  wire [3:0] din_t, multiplexer_2_out, q0, q1, q2, q3;

  or or_1 (clk, c, clr);
  Multiplexer #(.Selector_Bits(1), .Bits(4)) multiplexer_1 (.sel(clr), .in_0(Din), .in_1(4'b0000), .out(din_t));
  Demultiplexer #(.Selector_Bits(2)) demultiplexer_1 (
    .sel(WL), .in(WE), .out_0(demultiplexer_1_out_0), .out_1(demultiplexer_1_out_1),
    .out_2(demultiplexer_1_out_2), .out_3(demultiplexer_1_out_3));
  or or_2 (or_2_out, demultiplexer_1_out_0, clr);
  or or_3 (or_3_out, demultiplexer_1_out_1, clr);
  or or_4 (or_4_out, demultiplexer_1_out_2, clr);
  or or_5 (or_5_out, demultiplexer_1_out_3, clr);
  Register #(.Bits(4)) R0 (.D(din_t), .C(clk), .en(or_2_out), .Q(q0));
  Register #(.Bits(4)) R1 (.D(din_t), .C(clk), .en(or_3_out), .Q(q1));
  Register #(.Bits(4)) R2 (.D(din_t), .C(clk), .en(or_4_out), .Q(q2));
  Register #(.Bits(4)) R3 (.D(din_t), .C(clk), .en(or_5_out), .Q(q3));
  Multiplexer #(.Selector_Bits(2), .Bits(4)) multiplexer_2 (
    .sel(RL), .in_0(q0), .in_1(q1), .in_2(q2), .in_3(q3), .out(multiplexer_2_out));
  assign Dout = RE ? multiplexer_2_out : 4'bz;  // Driver driver_1
endmodule

/* Test case regfile:
c clr WE WL Din RE RL Dout
0 0 0 0 0 0 0 z
1 0 0 0 0 0 0 z
1 0 0 0 0 1 0 0
1 0 0 0 0 1 1 0
1 0 0 0 0 1 2 0
1 0 0 0 0 1 3 0
1 0 0 0 0 1 3 0
1 0 0 0 0 1 3 0
0 0 0 3 1 0 1 z
1 0 0 3 1 0 1 z
0 0 1 2 3 1 0 0
1 0 1 2 3 1 0 0
0 0 1 3 3 1 1 0
1 0 1 3 3 1 1 0
0 0 0 3 4 1 1 0
1 0 0 3 4 1 1 0
0 0 0 2 5 1 2 3
1 0 0 2 5 1 2 3
0 0 0 3 6 0 1 z
1 0 0 3 6 0 1 z
0 0 1 0 13 0 1 z
1 0 1 0 13 0 1 z
0 0 0 2 5 0 3 z
1 0 0 2 5 0 3 z
0 0 0 0 0 1 2 3
1 0 0 0 0 1 2 3
0 0 0 0 4 1 3 3
1 0 0 0 4 1 3 3
0 0 0 2 0 0 0 z
1 0 0 2 0 0 0 z
0 0 1 0 6 1 2 3
1 0 1 0 6 1 2 3
0 0 0 1 13 1 2 3
1 0 0 1 13 1 2 3
0 0 0 2 1 0 2 z
1 0 0 2 1 0 2 z
0 0 1 1 10 1 1 0
1 0 1 1 10 1 1 10
0 0 0 2 5 1 2 3
1 0 0 2 5 1 2 3
0 0 0 1 0 1 0 6
1 0 0 1 0 1 0 6
0 0 1 2 10 0 3 z
1 0 1 2 10 0 3 z
0 0 0 2 6 0 1 z
1 0 0 2 6 0 1 z
0 0 0 3 11 1 2 10
1 0 0 3 11 1 2 10
0 0 0 2 7 1 3 3
1 0 0 2 7 1 3 3
0 0 0 1 10 1 0 6
1 0 0 1 10 1 0 6
0 0 0 3 5 0 3 z
1 0 0 3 5 0 3 z
0 0 1 3 10 1 3 3
1 0 1 3 10 1 3 10
0 0 0 2 15 1 3 10
1 0 0 2 15 1 3 10
0 0 0 2 0 0 3 z
1 0 0 2 0 0 3 z
0 0 0 3 8 0 1 z
1 0 0 3 8 0 1 z
0 0 0 1 12 0 3 z
0 1 0 1 12 1 3 0
1 0 0 1 12 1 0 0
1 0 0 1 12 1 1 0
1 0 0 1 12 1 2 0
1 0 0 1 12 1 3 0
*/
