// Digital circuit HalfAdder.dig as structural Verilog
// Half adder used by the 4-bit successor.
// 半加器：S = A XOR B，C = A AND B。
module HalfAdder (
  input  A,
  input  B,
  output S,
  output C
);

  xor xor_1 (S, A, B);
  and and_1 (C, A, B);

  // Notes on the sheet:
  //   A: Addend bit A
  //   B: Addend bit B
  //   S: Sum bit (A XOR B)
  //   C: Carry bit (A AND B)
  //   Half Adder  S=A⊕B  C=A∧B
endmodule

/* Test case half-adder-truth:
A B C S
0 0 0 0
0 1 0 1
1 0 0 1
1 1 1 0
*/
