// Digital circuit Negation3.dig as structural Verilog
// Exercise 2 in a single file: 3-bit unsigned to 4-bit two's complement.
// -X = ~X + 1. Zero-extend, invert, then the full 4-bit successor (NOT + three half adders) is drawn with gates in this same circuit. No other .dig file is required.
module Negation3 (
  input  X_0,
  input  X_1,
  input  X_2,
  output Y_0,
  output Y_1,
  output Y_2,
  output Y_3
);

  wire and_1_out, and_2_out, not_1_out, not_2_out, not_3_out, not_4_out;

  not not_1 (not_1_out, X_0);
  not not_2 (not_2_out, X_1);
  not not_3 (not_3_out, X_2);
  not not_4 (not_4_out, 1'b0);
  not not_5 (Y_0, not_1_out);
  xor xor_1 (Y_1, not_2_out, not_1_out);
  and and_1 (and_1_out, not_2_out, not_1_out);
  xor xor_2 (Y_2, not_3_out, and_1_out);
  and and_2 (and_2_out, not_3_out, and_1_out);
  xor xor_3 (Y_3, not_4_out, and_2_out);
  // And and_3 has open pins: In_1=not_4_out, In_2=and_2_out, out=open

  // Notes on the sheet:
  //   X_0: LSB of the unsigned 3-bit input
  //   X_1: Input bit 1
  //   X_2: MSB of the unsigned 3-bit input
  //   Y_0: LSB of -X in 4-bit two's complement
  //   Y_3: Sign bit of -X
  //   Exercise 2  3-bit negation, all gates in this one file   -X = ~X + 1
  //   1. zero-extend to 4 bits, then invert
  //   2. inlined 4-bit successor (+1)
  //   bit0: S0 = NOT B0, C0 = B0
  //   bit1 half adder  S=A xor C, C=A and C
  //   bit2 half adder
  //   bit3 half adder
endmodule

/* Test case all-8-inputs:
# All 8 inputs. Y is the 4-bit two's complement of -X.
# 001 -> 1111 (-1); 010 -> 1110 (-2); 000 -> 0000; 111 -> 1001 (-7).
X_2 X_1 X_0 Y_3 Y_2 Y_1 Y_0
loop(n,8)
bits(3,n) bits(4,16-n)
end loop
*/
