// Digital circuit Successor4.dig as structural Verilog
// Full 4-bit successor (incrementer) S = A + 1, with carry-out.
// 完整 4 位后继器：最低位取反，高位用半加器级联进位；1111+1=10000。
module Successor4 (
  input  A_0,
  input  A_1,
  input  A_2,
  input  A_3,
  output S_0,
  output S_1,
  output S_2,
  output S_3,
  output C_out
);

  wire halfadder_1_c, halfadder_2_c;

  not not_1 (S_0, A_0);
  HalfAdder halfadder_1 (.A(A_1), .B(A_0), .S(S_1), .C(halfadder_1_c));
  HalfAdder halfadder_2 (.A(A_2), .B(halfadder_1_c), .S(S_2), .C(halfadder_2_c));
  HalfAdder halfadder_3 (.A(A_3), .B(halfadder_2_c), .S(S_3), .C(C_out));

  // Notes on the sheet:
  //   A_0: LSB of the 4-bit input
  //   S_0: LSB of A+1
  //   A_1: Input bit 1
  //   A_2: Input bit 2
  //   A_3: MSB of the 4-bit input
  //   S_1: Bit 1 of A+1
  //   S_2: Bit 2 of A+1
  //   S_3: Bit 3 of A+1
  //   C_out: Carry-out: 1111+1 becomes 10000
  //   Exercise 1  Full 4-bit successor  S = A + 1
  //   LSB: S0 = NOT A0,  C0 = A0  (HA with +1)
endmodule

/* Test case all-16-inputs:
# All 16 inputs. Full successor includes C_out so 15+1 = 10000.
A_3 A_2 A_1 A_0 C_out S_3 S_2 S_1 S_0
loop(n,16)
bits(4,n) bits(5,n+1)
end loop
*/
